# Fritzing sketch buttons (saved by Fritzing 1.0.2b)
breadboards: 1

parts:
  Part1 = Arduino Mega ADK (Rev3)
  S1 = Pushbutton [package="[THT]"]
  S2 = Pushbutton [package="[THT]"]
  R1 = Resistor [tolerance=±5% power=0.25W resistance=10k package=THT]
  R2 = Resistor [tolerance=±5% power=0.25W resistance=10k package=THT]
  LED1 = LED - 5mm [color="Red (633nm)" current=0.030A package="5 mm [THT]"]
  R3 = Resistor [tolerance=±5% power=0.25W resistance=220 package=THT]

nets:
  N1: Part1.D10_PWM, R3.Pin_1
  N2: Part1.5V, S1.Pin_3, S1.Pin_4, S2.Pin_3, S2.Pin_4
  N3: Part1.GND, R1.Pin_1, R2.Pin_1, LED1.cathode
  N4: Part1.D5_PWM, S2.Pin_1, S2.Pin_2, R1.Pin_0
  N5: Part1.D6_PWM, S1.Pin_1, S1.Pin_2, R2.Pin_0
  N6: LED1.anode, R3.Pin_0
